# Fritzing sketch Status-LED-Shield (saved by Fritzing 0.9.3b)
circuit board: 1.47071cm x 1.11537cm

parts:
  LED = RGB LED (com. anode, rbg) [package="5 mm [THT]"]
  R2 = Resistor [tolerance=±5% resistance=220 package=THT]
  R1 = Resistor [tolerance=±5% resistance=220 package=THT]
  P3 = female pin header, 4 pins [form="♀ (female)"]

nets:
  N1: LED.red_cathode, R1.Pin_1
  N2: LED.common_anode, P3.pin1
  N3: LED.green_cathode, R2.Pin_1
  N4: R2.Pin_0, P3.pin3
  N5: R1.Pin_0, P3.pin2

notes:
  Shield v1.0
  Status LED
  VCC
  D5
  D6
  GND
